# Fritzing sketch Tinny-Injector (saved by Fritzing 0.9.3b)
circuit board: 5cm x 3.5cm
breadboards: 1

parts:
  U1 = attiny85 [package=dip]
  U2 = Sharp PC817 [package=THT]
  Q1 = MOSFET-NCHANNEL [package=to220v]
  R1 = Resistor [tolerance=±5% resistance=1k package=THT]
  R2 = Resistor [tolerance=±5% resistance=1k package=THT]
  LED1 = LED - 5mm [color="Red (633nm)" package="5 mm [THT]"]
  R3 = Resistor [tolerance=±5% resistance=100 package=THT]
  R4 = Resistor [tolerance=±5% resistance=1k package=THT]
  D1 = Rectifier Diode [part_number=1N4001 package="300 mil [THT]"]
  U3 = Voltage Regulator - 5V [package="TO220 [THT]"]
  J2 = female pin header, 4 pins [form="♀ (female)"]
  J1 = female pin header, 2 pins [form="♀ (female)"]
  J3 = female pin header, 1 pin [form="♀ (female)"]
  D2 = Rectifier Diode [part_number=1N4001 package="300 mil [THT]"]  # not connected

nets:
  N1: U1.Pin_3, J2.pin2
  GND: U1.Pin_4, U2.Pin_2, Q1.S, LED1.cathode, R4.Pin_0, U3.GND, J2.pin4, J1.pin2
  N2: U1.Pin_6, R1.Pin_0, R2.Pin_1
  N3: U1.Pin_7, J2.pin1
  N4: U1.Pin_8, U3.output_voltage, J2.pin3
  N5: U2.Pin_1, R1.Pin_1
  N6: U2.Pin_4, D1.cathode, U3.input_voltage
  N7: U2.Pin_3, R3.Pin_0, R4.Pin_1
  N8: Q1.G, R3.Pin_1
  N9: Q1.D, J3.pin1
  N10: R2.Pin_0, LED1.anode
  N11: D1.anode, J1.pin1

notes:
  By AB
